// Logisim project PC.circ as structural Verilog: 1 circuit, main circuit VonNeumannPC_x16
module VonNeumannPC_x16 (
);

  wire ALU_or_Data, clk, EQ, GE, GT, LE, LT, mux8_1_out_10, mux_x_1_out_4, mux_x_2_out_4, mux_x_3_out_4,
       mux_x_4_out_4, NE;
  wire [1:0] rom_1_data_3;
  wire [2:0] rom_1_data;
  wire [14:0] alu_16_1_out_7;
  wire [14:3] rom_1_data_2;
  wire [15:0] mux_x16_1_out_4, mux_x16_2_out_4, pc_x16_1_out_4, ram_1_dout, reg_x16_1_out_4, reg_x16_2_out_4;

  Clock clock_1 (.out(clk));
  // Probe on {ALU_or_Data, rom_1_data_2[14:10], rom_1_data_3, rom_1_data_2[7:3], rom_1_data}
  mux8 mux8_1 (
    .in_9(rom_1_data), .in_1(1'b1), .in_2(LE), .in_3(NE), .in_4(LT), .in_5(GE), .in_6(EQ), .in_7(GT),
    .out_10(mux8_1_out_10));  // open: in_8
  mux_x16 mux_x16_1 (.in_1(rom_1_data_2[12]), .in_2(ram_1_dout), .in_3(reg_x16_2_out_4), .out_4(mux_x16_1_out_4));
  alu_16 alu_16_1 (
    .Op_code(rom_1_data_3), .in_2(rom_1_data_2[7]), .in_3(rom_1_data_2[6]), .y(reg_x16_1_out_4),
    .in_6(mux_x16_1_out_4), .u(rom_1_data_2[10]), .out_7({LT, alu_16_1_out_7}));
  or16_x or16_x_1 (.in_1({LT, alu_16_1_out_7}), .out_2(NE));
  not_x not_x_1 (.in_1(LT), .out_2(GE));
  not_x not_x_2 (.in_1(NE), .out_2(EQ));
  // Probe on {ALU_or_Data, rom_1_data_2[14:10], rom_1_data_3, rom_1_data_2[7:3], rom_1_data}
  or_x or_x_1 (.in_1(EQ), .in_2(LT), .out_3(LE));
  ROM #(.addrWidth(16), .dataWidth(16)) rom_1 (
    .addr(pc_x16_1_out_4),
    .data({ALU_or_Data, rom_1_data_2[14:10], rom_1_data_3, rom_1_data_2[7:3], rom_1_data}));
  // Probe on mux_x_1_out_4
  mux_x mux_x_1 (.Select(ALU_or_Data), .D1(mux8_1_out_10), .D0(1'b0), .out_4(mux_x_1_out_4));
  mux_x16 mux_x16_2 (
    .in_1(ALU_or_Data), .in_2({LT, alu_16_1_out_7}),
    .in_3({ALU_or_Data, rom_1_data_2[14:10], rom_1_data_3, rom_1_data_2[7:3], rom_1_data}),
    .out_4(mux_x16_2_out_4));
  mux_x mux_x_2 (.Select(ALU_or_Data), .D1(rom_1_data_2[5]), .D0(1'b1), .out_4(mux_x_2_out_4));
  mux_x mux_x_3 (.Select(ALU_or_Data), .D1(rom_1_data_2[4]), .D0(1'b0), .out_4(mux_x_3_out_4));
  mux_x mux_x_4 (.Select(ALU_or_Data), .D1(rom_1_data_2[3]), .D0(1'b0), .out_4(mux_x_4_out_4));
  not_x not_x_3 (.in_1(LE), .out_2(GT));
  // Probe on mux_x16_2_out_4
  // Probe on mux_x_2_out_4
  // Probe on mux_x_3_out_4
  // Probe on mux_x_4_out_4
  // Probe on pc_x16_1_out_4
  RAM #(.addrWidth(16), .dataWidth(16), .trigger("falling")) ram_1 (
    .addr(reg_x16_2_out_4), .we(mux_x_4_out_4), .oe(1'b1), .clk(clk), .din(mux_x16_2_out_4), .dout(ram_1_dout));
  reg_x16 reg_x16_1 (.in_1(clk), .load(mux_x_3_out_4), .data(mux_x16_2_out_4), .out_4(reg_x16_1_out_4));
  reg_x16 reg_x16_2 (.in_1(clk), .load(mux_x_2_out_4), .data(mux_x16_2_out_4), .out_4(reg_x16_2_out_4));
  pc_x16 pc_x16_1 (.load(mux_x_1_out_4), .in_3(reg_x16_2_out_4), .in_1(clk), .out_4(pc_x16_1_out_4));
  // Probe on reg_x16_1_out_4
  // Probe on reg_x16_2_out_4
  // Probe on ram_1_dout

  // Notes on the sheet:
  //   Instruction
  //   Reg D
  //   A*
  //   Reg A
  //   (ALU) Jump Flag
  //   (ALU) Result
  //   (ALU) output to A flag
  //   ( ALU) output to D flag
  //   (ALU) output to A*
  //   memory data at address
  //   address
  //   Reg A
  //   D
  //   A
endmodule
